// Digital circuit instruction_mem.dig as structural Verilog
module instruction_mem (
  input  [31:0] _32b__ADDR,
  input  _1b__Enable,
  output [31:0] _32b__Out
);

  ROM #(.AddrBits(8), .Bits(32)) rom_1 (.A(_32b__ADDR[7:0]), .sel(_1b__Enable), .D(_32b__Out));

  // Notes on the sheet:
  //   contents of rom_1 (hex, n*v repeats v):
  //   4*61616161
endmodule
