// Digital circuit main.dig as structural Verilog
module main (
  input  clock,
  input  pc_reset
);

  wire ALU_Control_p2, ALU_Control_p5, APC, branch, ex_mem_1_mem_memread, ex_mem_1_mem_memtoreg,
       ex_mem_1_mem_memwrite, ex_mem_1_wb_regwrite, id_ex_1_p17, id_ex_1_p18, id_ex_1_p20, id_ex_1_p21,
       id_ex_1_p22, id_ex_1_p23, id_ex_1_p24, if_id_1_p2, jump, mem_wb_1_wb_memtoreg, mem_wb_1_wb_regwrite,
       stall_1_p1, stall_1_p2, stall_1_p5, ULA_p5;
  wire [1:0] FA, FB;
  wire [4:0] ALU_Control_p1, ex_mem_1_mem_dstaddr, mem_wb_1_wb_dstaddr, multiplexer_5_out, stall_1_p6,
       undriven_2;
  wire [5:0] if_id_1_p4;
  wire [8:0] multiplexer_4_out, UC_b;
  wire [25:0] jump_constant;
  wire [31:0] add_1_s, add_2_s, Banco_de_registradores_rs_data, Banco_de_registradores_rt_data,
       barrelshifter_1_out, bitextender_1_out, Constant, ex_mem_1_mem_rtdata, id_ex_1_p25, Mem_result,
       mem_wb_1_wb_readdata, mem_wb_1_wb_result, \Memória_de_dados_data ,
       \Memória_de_instruções_instruction , multiplexer_1_out, multiplexer_2_out, multiplexer_3_out,
       multiplexer_6_out, multiplexer_7_out, multiplexer_8_out, pc_1_address, R31, ULA_p6, undriven, WB;

  Add #(.Bits(32)) add_1 (.a(pc_1_address), .b(32'h4), .c_i(1'b0), .s(add_1_s));  // open: c_o
  BarrelShifter #(.Bits(32)) barrelshifter_1 (.in(Constant), .shift(6'b000010), .out(barrelshifter_1_out));
  PC pc_1 (.clock(clock), .write(multiplexer_2_out), .reset(pc_reset), .enable(APC), .address(pc_1_address));
  Add #(.Bits(32)) add_2 (.a(add_1_s), .b(barrelshifter_1_out), .c_i(1'b0), .s(add_2_s));  // open: c_o
  Multiplexer #(.Bits(32)) multiplexer_1 (.sel(branch), .in_0(add_1_s), .in_1(add_2_s), .out(multiplexer_1_out));
  Multiplexer #(.Bits(32)) multiplexer_2 (
    .sel(jump), .in_0(multiplexer_1_out), .in_1({pc_1_address[31:28], jump_constant, 2'b00}),
    .out(multiplexer_2_out));
  instruction_mem \Memória_de_instruções  (.address(pc_1_address), .instruction(\Memória_de_instruções_instruction ));
  Multiplexer #(.Bits(32)) multiplexer_3 (
    .sel(stall_1_p2), .in_0(\Memória_de_instruções_instruction ), .in_1({32{1'b0}}), .out(multiplexer_3_out));
  // IF_ID if_id_1: pin names not known; wires that end beside it: multiplexer_3_out, if_id_1_p2, clock, {if_id_1_p4, jump_constant}
  or or_1 (if_id_1_p2, ~stall_1_p1, stall_1_p2);  // Or
  Control UC (
    .RgD(UC_b[0]), .AluS(UC_b[1]), .MTR(UC_b[2]), .RW(UC_b[3]), .MR(UC_b[4]), .MW(UC_b[5]), .B(UC_b[6]),
    .AO_1(UC_b[7]), .AO_0(UC_b[8]), .J(jump), .APC(APC), .Op(if_id_1_p4));
  _32x32 Banco_de_registradores (
    .reg_write(mem_wb_1_wb_regwrite), .write_data(WB), .rs_addr(jump_constant[25:21]),
    .rt_addr(jump_constant[20:16]), .rd_addr(mem_wb_1_wb_dstaddr), .clock(clock),
    .rs_data(Banco_de_registradores_rs_data), .rt_data(Banco_de_registradores_rt_data), .R31(R31));
  BitExtender #(.inputBits(16), .outputBits(32)) bitextender_1 (.in(jump_constant[15:0]), .out(bitextender_1_out));
  Seven_Seg_Hex seven_seg_hex_1 (.d(R31[19:16]), .dp(1'b0));
  Multiplexer #(.Bits(9)) multiplexer_4 (.sel(stall_1_p1), .in_0(UC_b), .in_1({9{1'b0}}), .out(multiplexer_4_out));
  Seven_Seg_Hex seven_seg_hex_2 (.d(R31[15:12]), .dp(1'b0));
  // Stall stall_1: pin names not known; wires that end beside it: stall_1_p1, stall_1_p2, jump_constant[25:21], jump_constant[20:16], stall_1_p5, stall_1_p6, branch
  Seven_Seg_Hex seven_seg_hex_3 (.d(R31[11:8]), .dp(1'b0));
  // ID_EX id_ex_1: pin names not known; wires that end beside it: jump, multiplexer_4_out[3], multiplexer_4_out[2], multiplexer_4_out[4], multiplexer_4_out[5], multiplexer_4_out[6], multiplexer_4_out[0], multiplexer_4_out[1], multiplexer_4_out[8:7], Banco_de_registradores_rs_data, Banco_de_registradores_rt_data, bitextender_1_out, jump_constant[25:21], jump_constant[20:16], jump_constant[15:11], jump_constant[5:0], id_ex_1_p17, id_ex_1_p18, stall_1_p5, id_ex_1_p20, id_ex_1_p21, id_ex_1_p22, id_ex_1_p23, id_ex_1_p24, id_ex_1_p25
  Seven_Seg_Hex seven_seg_hex_4 (.d(R31[7:4]), .dp(1'b0));
  Seven_Seg_Hex seven_seg_hex_5 (.d(R31[3:0]), .dp(1'b0));
  Multiplexer #(.Bits(5)) multiplexer_5 (
    .sel(id_ex_1_p22), .in_0(stall_1_p6), .in_1(ALU_Control_p1), .out(multiplexer_5_out));
  Multiplexer #(.Selector_Bits(2), .Bits(32)) multiplexer_6 (
    .sel(FB), .in_0(undriven), .in_1(WB), .in_2(Mem_result), .in_3(Mem_result), .out(multiplexer_6_out));
  // ALU_Control ALU_Control: pin names not known; wires that end beside it: ALU_Control_p1, ALU_Control_p2, id_ex_1_p24, ALU_Control_p2, ALU_Control_p5
  Multiplexer #(.Bits(32)) multiplexer_7 (
    .sel(id_ex_1_p23), .in_0(multiplexer_6_out), .in_1(Constant), .out(multiplexer_7_out));
  Multiplexer #(.Selector_Bits(2), .Bits(32)) multiplexer_8 (
    .sel(FA), .in_0(id_ex_1_p25), .in_1(WB), .in_2(Mem_result), .in_3(Mem_result), .out(multiplexer_8_out));
  // ula ULA: pin names not known; wires that end beside it: ALU_Control_p5, multiplexer_8_out, multiplexer_7_out, {6{1'b0}}, ULA_p5, ULA_p6
  forwarding_unit Unidade_de_forwarding (
    .RS(undriven_2), .RT(stall_1_p6), .EX_MEM_dest(ex_mem_1_mem_dstaddr), .MEM_WB_dest(mem_wb_1_wb_dstaddr),
    .EX_MEM_rw(ex_mem_1_wb_regwrite), .MEM_WB_rw(mem_wb_1_wb_regwrite), .FA(FA), .FB(FB));
  and and_1 (branch, id_ex_1_p21, ULA_p5);
  EX_MEM ex_mem_1 (
    .EX_regWrite(id_ex_1_p17), .EX_memRead(stall_1_p5), .EX_memWrite(id_ex_1_p20), .EX_memToReg(id_ex_1_p18),
    .EX_result(ULA_p6), .EX_rtData(multiplexer_6_out), .EX_dstAddr(multiplexer_5_out), .clock(clock),
    .WB_regWrite(ex_mem_1_wb_regwrite), .MEM_memRead(ex_mem_1_mem_memread),
    .MEM_memWrite(ex_mem_1_mem_memwrite), .MEM_memToReg(ex_mem_1_mem_memtoreg), .MEM_result(Mem_result),
    .MEM_rtData(ex_mem_1_mem_rtdata), .MEM_dstAddr(ex_mem_1_mem_dstaddr));
  memory_24x32 \Memória_de_dados  (
    .address(Mem_result[23:0]), .write_data(ex_mem_1_mem_rtdata), .mem_write(ex_mem_1_mem_memwrite),
    .mem_read(ex_mem_1_mem_memread), .clock(clock), .data(\Memória_de_dados_data ));
  MEM_WB mem_wb_1 (
    .MEM_regWrite(ex_mem_1_wb_regwrite), .MEM_memToReg(ex_mem_1_mem_memtoreg),
    .MEM_readData(\Memória_de_dados_data ), .MEM_result(Mem_result), .MEM_dstAddr(ex_mem_1_mem_dstaddr),
    .clock(clock), .WB_regWrite(mem_wb_1_wb_regwrite), .WB_memToReg(mem_wb_1_wb_memtoreg),
    .WB_readData(mem_wb_1_wb_readdata), .WB_result(mem_wb_1_wb_result), .WB_dstAddr(mem_wb_1_wb_dstaddr));
  Multiplexer #(.Bits(32)) multiplexer_9 (
    .sel(mem_wb_1_wb_memtoreg), .in_0(mem_wb_1_wb_result), .in_1(mem_wb_1_wb_readdata), .out(WB));

  // Notes on the sheet:
  //   addi $ra, $zero, 5
  //   loop:
  //   beq $ra, $zero, done
  //   addi $ra, $ra, -1
  //   j loop
  //   done:
  //   Reg Destino
  //   MEM/WB_Dest
  //   MEM/WB_RegWrite
endmodule
